# Fritzing sketch schema_electrique (saved by Fritzing 0.9.9b)
breadboards: 1

parts:
  5V = Arduino Mega 2560 (Rev3)
  5V_2 = Power plug
  M10 = fc-51 [package=THT]
  M11 = fc-51 [package=THT]
  M12 = fc-51 [package=THT]
  M13 = fc-51 [package=THT]
  M14 = fc-51 [package=THT]
  M21 = Dagu DGServo 9g (Top view) [part_number=RS001B]
  M26 = Dagu DGServo 9g (Top view) [part_number=RS001B]
  M27 = Dagu DGServo 9g (Top view) [part_number=RS001B]
  M28 = Dagu DGServo 9g (Top view) [part_number=RS001B]
  M29 = Dagu DGServo 9g (Top view) [part_number=RS001B]
  SM1 = 28BYJ-48 Stepper Motor [part_number=28BYJ-48]
  Driver1 = 28BYJ-48 Driver Module [part_number=ULN2003 package=THT]
  Driver2 = 28BYJ-48 Driver Module [part_number=ULN2003 package=THT]
  SM2 = 28BYJ-48 Stepper Motor [part_number=28BYJ-48]
  Driver3 = 28BYJ-48 Driver Module [part_number=ULN2003 package=THT]
  SM3 = 28BYJ-48 Stepper Motor [part_number=28BYJ-48]
  Driver4 = 28BYJ-48 Driver Module [part_number=ULN2003 package=THT]
  SM4 = 28BYJ-48 Stepper Motor [part_number=28BYJ-48]
  LCD1 = LCD screen
  Composant1 = 4x4 Keypad [part_number=101207]
  LCM1602_IIC1 = LCM1602 IIC [part_number="LCM1602 IIC" chip_label="LCM1602 IIC" package="DIP (Dual Inline) [THT]"]

nets:
  N1: 5V.SCL, LCM1602_IIC1.SCL
  N2: 5V.SDA, LCM1602_IIC1.SDA
  N3: 5V.D13_PWM, M29.pulse
  N4: 5V.D12_PWM, M28.pulse
  N5: 5V.D11_PWM, M27.pulse
  N6: 5V.D10_PWM, M26.pulse
  N7: 5V.D9_PWM, M21.pulse
  GND: 5V.GND, 5V_2.GND, M10.pin2, M11.pin2, M12.pin2, M13.pin2, M14.pin2, M21.gnd, M26.gnd, M27.gnd, M28.gnd, M29.gnd, Driver1.GND, Driver2.GND, Driver3.GND, Driver4.GND, Composant1.4, Composant1.5, LCM1602_IIC1.GND
  N8: 5V.D2_PWM, M13.pin1
  N9: 5V.D3_PWM, M12.pin1
  N10: 5V.D4_PWM, M11.pin1
  N11: 5V.D5_PWM, M10.pin1
  N12: 5V.D6_PWM, M14.pin1
  N13: 5V.5V, Driver2.IN4, Driver4.IN1
  N14: 5V.D22, Driver2.IN3
  N15: 5V.D23, Driver4.IN2
  N16: 5V.D24, Driver2.IN2
  N17: 5V.D25, Driver4.IN3
  N18: 5V.D26, Driver2.IN1
  N19: 5V.D27, Driver4.IN4
  N20: 5V.D28, Driver1.IN4
  N21: 5V.D29, Driver3.IN1
  N22: 5V.D30, Driver1.IN3
  N23: 5V.D31, Driver3.IN2
  N24: 5V.D32, Driver1.IN2
  N25: 5V.D33, Driver3.IN3
  N26: 5V.D34, Driver1.IN1
  N27: 5V.D35, Driver3.IN4
  N28: 5V.D48, Composant1.8
  N29: 5V.D49, Composant1.1
  N30: 5V.D50, Composant1.7
  N31: 5V.D51, Composant1.2
  N32: 5V.D52, Composant1.6
  N33: 5V.D53, Composant1.3
  VCC: 5V_2.VCC, M10.pin3, M11.pin3, M12.pin3, M13.pin3, M14.pin3, M21.vcc, M26.vcc, M27.vcc, M28.vcc, M29.vcc, Driver1.Vmotor, Driver2.Vmotor, Driver3.Vmotor, Driver4.ON/OFF, LCM1602_IIC1.VCC
  N34: SM1.blue-pin, Driver1.blue-pin
  N35: SM1.pink-pin, Driver1.pink-pin
  N36: SM1.yellow-pin, Driver1.yellow-pin
  N37: SM1.orange-pin, Driver1.orange-pin
  N38: SM1.red-pin, Driver1.red-pin
  N39: Driver2.blue-pin, SM2.blue-pin
  N40: Driver2.pink-pin, SM2.pink-pin
  N41: Driver2.yellow-pin, SM2.yellow-pin
  N42: Driver2.orange-pin, SM2.orange-pin
  N43: Driver2.red-pin, SM2.red-pin
  N44: Driver3.blue-pin, SM3.blue-pin
  N45: Driver3.pink-pin, SM3.pink-pin
  N46: Driver3.yellow-pin, SM3.yellow-pin
  N47: Driver3.orange-pin, SM3.orange-pin
  N48: Driver3.red-pin, SM3.red-pin
  N49: Driver4.blue-pin, SM4.blue-pin
  N50: Driver4.pink-pin, SM4.pink-pin
  N51: Driver4.yellow-pin, SM4.yellow-pin
  N52: Driver4.orange-pin, SM4.orange-pin
  N53: Driver4.red-pin, SM4.red-pin
  VSS: LCD1.VSS, LCM1602_IIC1.VSS
  VDD: LCD1.VDD, LCM1602_IIC1.VDD
  N54: LCD1.V0, LCM1602_IIC1.V0
  N55: LCD1.RS, LCM1602_IIC1.RS
  N56: LCD1.R/W, LCM1602_IIC1.RW
  N57: LCD1.E, LCM1602_IIC1.E
  N58: LCD1.DB4, LCM1602_IIC1.D4
  N59: LCD1.DB5, LCM1602_IIC1.D5
  N60: LCD1.DB6, LCM1602_IIC1.D6
  N61: LCD1.DB7, LCM1602_IIC1.D7
  N62: LCD1.LED+, LCM1602_IIC1.A
  N63: LCD1.LED-, LCM1602_IIC1.K
  N64: LCM1602_IIC1.LED_A, LCM1602_IIC1.LED_B

custom parts:
  28BYJ-48 Stepper Motor: Unipolar Stepper Motor 28BYJ-48 Top coil - pink & orange Bottom coil - blue & yellow Common rail - red Connector pins: blue - pink - yellow - orange - red
  28BYJ-48 Driver Module: ULN2003 Driver Module for the 28BYJ-48 Unipolar Stepper Motor LED A - Blue wire - Bottom coil left LED B - Pink wire - Top coil left LED C - Yellow wire - Bottom coil right LED D - Orange wire - Top coil right Common rail - red Connector pins: blue - pink - yellow - orange - red Control pins - IN1 to IN4 Power pins - GND & Vmotor (5-12V) On/Off jumper (if removed, power to motor is cut).
  4x4 Keypad: Matrix membrane keypad 4x4
  LCM1602 IIC: I2C-Module to use a 1602 or 2004 LCD on with the wire.h libory Serial LCD Modul
